# Fritzing sketch DisplayLiFi-proto1 (saved by Fritzing 0.9.1b)
breadboards: 1

parts:
  Photo_IC_Diode_S9648-100 = LED - 5mm [color="Red (633nm)" package="5 mm [THT]"]
  Part1 = Arduino Pro Mini v13
  R1 = Resistor [tolerance=±5% resistance=1k package=THT]
  R2 = Resistor [tolerance=±5% resistance=100 package=THT]

nets:
  N1: Photo_IC_Diode_S9648-100.cathode, Part1.A0, R2.Pin_1
  N2: Photo_IC_Diode_S9648-100.anode, R1.Pin_1
  N3: Part1.GND, R2.Pin_0
  N4: Part1.VCC, R1.Pin_0
